# Fritzing sketch Voice Your Opinion (saved by Fritzing 0.7.4b)
breadboards: 1

parts:
  Arduino1 = Arduino
  LED1 = LED - 5mm [color="Red (633nm)" package="5 mm [THT]"]
  LED2 = LED - 5mm [color="Red (633nm)" package="5 mm [THT]"]
  LED3 = LED - 5mm [color="Red (633nm)" package="5 mm [THT]"]
  LED4 = LED - 5mm [color="Red (633nm)" package="5 mm [THT]"]
  LED5 = LED - 5mm [color="Red (633nm)" package="5 mm [THT]"]
  LED6 = LED - 5mm [color="Red (633nm)" package="5 mm [THT]"]
  LED7 = LED - 5mm [color="Red (633nm)" package="5 mm [THT]"]
  LED8 = LED - 5mm [color="Red (633nm)" package="5 mm [THT]"]
  LED9 = LED - 5mm [color="Red (633nm)" package="5 mm [THT]"]
  Part1 = Breakout Board for Electret Microphone

nets:
  GND: Arduino1.GND, LED6.cathode, LED7.cathode, LED8.cathode, LED9.cathode, Part1.GND
  N1: Arduino1.D10, LED9.anode
  N2: Arduino1.D9, LED8.anode
  N3: Arduino1.D8, LED7.anode
  N4: Arduino1.D7, LED6.anode
  N5: Arduino1.D6, LED5.anode
  N6: Arduino1.D5, LED4.anode
  N7: Arduino1.D4, LED3.anode
  N8: Arduino1.D3, LED2.anode
  N9: Arduino1.D2, LED1.anode
  3V3: Arduino1.3V3, Part1.VCC
  N10: Arduino1.A1, Part1.AUD
  N11: LED1.cathode, LED2.cathode, LED3.cathode, LED4.cathode, LED5.cathode
